# Fritzing sketch fumlebræt (saved by Fritzing 0.9.3b)
circuit board: 8.46667cm x 5.64444cm
breadboards: 1

parts:
  Part1 = Arduino Mega 2560 (Rev3)
  R1 = Resistor [tolerance=±5% resistance=100k package=THT]
  R2 = Resistor [tolerance=±5% resistance=220 package=THT]
  R3 = Resistor [tolerance=±5% resistance=220 package=THT]
  LED2 = LED - 5mm [color="Red (633nm)" package="5 mm [THT]"]
  LED3 = LED - 5mm [color="Red (633nm)" package="5 mm [THT]"]
  LED4 = LED - 5mm [color="Red (633nm)" package="5 mm [THT]"]

nets:
  N1: Part1.D12_PWM, R1.Pin_0
  N2: Part1.D11_PWM, R2.Pin_0
  N3: Part1.D10_PWM, R3.Pin_0
  N4: Part1.GND, LED2.anode, LED3.anode, LED4.anode
  N5: R1.Pin_1, LED3.cathode
  N6: R2.Pin_1, LED2.cathode
  N7: R3.Pin_1, LED4.cathode
